# Fritzing sketch board (saved by Fritzing 0.9.3b)
breadboards: 1

parts:
  Raspberry_Pi_1 = Raspberry Pi 3 [part_number=RPI-3-V1.2]
  R1 = Resistor [tolerance=±5% resistance=470 package="0402 [SMD]"]
  Q1 = NPN-Transistor [part_number=2N2222A package="TO92 [THT]"]
  D1 = Schottky Diode [part_number=1N5817 package="300 mil [THT]"]
  M1 = DC Motor

nets:
  N1: Raspberry_Pi_1.GND, Q1.E
  N2: Raspberry_Pi_1.GPIO18, R1.Pin_0
  N3: Raspberry_Pi_1.5V, D1.cathode, M1.pin_1
  N4: R1.Pin_1, Q1.B
  N5: Q1.C, D1.anode, M1.pin_2
